// Logisim project Guia_0605.circ as structural Verilog
module G06_05 (
  input  a,
  input  b,
  input  c,
  output out_4
);

  wire and_1_out, not_1_out;

  and and_1 (and_1_out, b, c);
  not not_1 (not_1_out, a);
  nor nor_1 (out_4, and_1_out, not_1_out);
endmodule
