// Logisim project Guia_0606.circ as structural Verilog
module G06_06 (
  input  a,
  input  b,
  input  c,
  input  d,
  output out_5
);

  wire and_1_out, not_1_out;

  and and_1 (and_1_out, b, d);
  not not_1 (not_1_out, a);
  nor nor_1 (out_5, and_1_out, not_1_out);
endmodule
