// Logisim project Guia_0701.circ as structural Verilog
module G07_01 (
  input  a,
  input  b,
  input  in_3,
  output out_4,
  output out_5
);

  wire and_1_out, nand_1_out, not_1_out;

  nand nand_1 (nand_1_out, a, b);
  not not_1 (not_1_out, in_3);
  and and_1 (and_1_out, a, b);
  and and_2 (out_4, nand_1_out, not_1_out);
  and and_3 (out_5, and_1_out, in_3);
endmodule
