// Logisim project Guia_0702.circ as structural Verilog
module G07_02 (
  input  a,
  input  b,
  input  chave,
  output out_4
);

  wire and_1_out, and_2_out, nor_1_out, not_1_out, or_1_out;

  nor nor_1 (nor_1_out, a, b);
  not not_1 (not_1_out, chave);
  or or_1 (or_1_out, a, b);
  and and_1 (and_1_out, nor_1_out, not_1_out);
  and and_2 (and_2_out, or_1_out, chave);
  or or_2 (out_4, and_1_out, and_2_out);
endmodule
