// Logisim project Guia_0704.circ as structural Verilog
module G07_04 (
  input  a,
  input  b,
  input  chave1,
  input  chave2,
  output out_5
);

  wire and_1_out, and_2_out, and_3_out, and_4_out, and_5_out, and_6_out, nor_1_out, not_1_out, not_2_out,
       not_3_out, or_1_out, or_2_out, or_3_out, xnor_1_out, xor_1_out;

  nor nor_1 (nor_1_out, a, b);
  not not_1 (not_1_out, chave1);
  or or_1 (or_1_out, a, b);
  xor xor_1 (xor_1_out, a, b);
  not not_2 (not_2_out, chave1);
  xnor xnor_1 (xnor_1_out, a, b);
  and and_1 (and_1_out, nor_1_out, not_1_out);
  and and_2 (and_2_out, or_1_out, chave1);
  and and_3 (and_3_out, xor_1_out, not_2_out);
  and and_4 (and_4_out, xnor_1_out, chave1);
  or or_2 (or_2_out, and_1_out, and_2_out);
  not not_3 (not_3_out, chave2);
  or or_3 (or_3_out, and_3_out, and_4_out);
  and and_5 (and_5_out, or_2_out, not_3_out);
  and and_6 (and_6_out, or_3_out, chave2);
  or or_4 (out_5, and_5_out, and_6_out);
endmodule
