// Logisim project Guia_0705.circ as structural Verilog
module G07_05 (
  input  a,
  input  b,
  input  chave1,
  input  chave2,
  input  chave3,
  output out_6
);

  wire and_1_out, and_2_out, and_3_out, and_4_out, and_5_out, and_6_out, and_7_out, and_8_out, and_9_out,
       and_10_out, and_11_out, and_12_out, and_13_out, and_14_out, and_15_out, nand_1_out, nor_1_out,
       not_1_out, not_2_out, not_3_out, not_4_out, not_5_out, not_6_out, not_7_out, not_8_out, not_9_out,
       or_1_out, or_2_out, or_3_out, or_4_out, or_5_out, or_6_out, or_7_out, xnor_1_out, xor_1_out;

  not not_1 (not_1_out, a);
  not not_2 (not_2_out, chave1);
  not not_3 (not_3_out, b);
  and and_1 (and_1_out, a, b);
  not not_4 (not_4_out, chave1);
  nand nand_1 (nand_1_out, a, b);
  or or_1 (or_1_out, a, b);
  not not_5 (not_5_out, chave1);
  nor nor_1 (nor_1_out, a, b);
  xor xor_1 (xor_1_out, a, b);
  not not_6 (not_6_out, chave1);
  xnor xnor_1 (xnor_1_out, a, b);
  and and_2 (and_2_out, not_1_out, not_2_out);
  and and_3 (and_3_out, not_3_out, chave1);
  and and_4 (and_4_out, and_1_out, not_4_out);
  and and_5 (and_5_out, nand_1_out, chave1);
  and and_6 (and_6_out, or_1_out, not_5_out);
  and and_7 (and_7_out, nor_1_out, chave1);
  and and_8 (and_8_out, xor_1_out, not_6_out);
  and and_9 (and_9_out, xnor_1_out, chave1);
  or or_2 (or_2_out, and_2_out, and_3_out);
  not not_7 (not_7_out, chave2);
  or or_3 (or_3_out, and_4_out, and_5_out);
  or or_4 (or_4_out, and_6_out, and_7_out);
  not not_8 (not_8_out, chave2);
  or or_5 (or_5_out, and_8_out, and_9_out);
  and and_10 (and_10_out, or_2_out, not_7_out);
  and and_11 (and_11_out, or_3_out, chave2);
  and and_12 (and_12_out, or_4_out, not_8_out);
  and and_13 (and_13_out, or_5_out, chave2);
  or or_6 (or_6_out, and_10_out, and_11_out);
  not not_9 (not_9_out, chave3);
  or or_7 (or_7_out, and_12_out, and_13_out);
  and and_14 (and_14_out, or_6_out, not_9_out);
  and and_15 (and_15_out, or_7_out, chave3);
  or or_8 (out_6, and_14_out, and_15_out);
endmodule
