// Logisim project Guia_0801.circ as structural Verilog
module G08_01 (
  input  a4,
  input  a3,
  input  a2,
  input  a1,
  input  b4,
  input  b3,
  input  b2,
  input  b1,
  output out_9,
  output out_10,
  output out_11,
  output out_12,
  output out_13
);

  wire half_adder_1_s1, half_adder_2_s0, half_adder_2_s1, half_adder_3_s1, half_adder_4_s0, half_adder_4_s1,
       half_adder_5_s0, half_adder_5_s1, half_adder_6_s1, half_adder_7_s1, half_adder_8_s0, half_adder_8_s1,
       or_2_out, or_3_out, s11_out;

  or or_1 (out_9, half_adder_1_s1, half_adder_2_s1);
  Half_Adder half_adder_1 (.s0(out_10), .s1(half_adder_1_s1), .a(half_adder_2_s0), .b(or_2_out));
  Half_Adder half_adder_2 (.s0(half_adder_2_s0), .s1(half_adder_2_s1), .a(a4), .b(b4));
  or or_2 (or_2_out, half_adder_3_s1, half_adder_4_s1);
  Half_Adder half_adder_3 (.s0(out_11), .s1(half_adder_3_s1), .a(half_adder_4_s0), .b(or_3_out));
  Half_Adder half_adder_4 (.s0(half_adder_4_s0), .s1(half_adder_4_s1), .a(a3), .b(b3));
  or or_3 (or_3_out, half_adder_6_s1, half_adder_5_s1);
  Half_Adder half_adder_5 (.s0(half_adder_5_s0), .s1(half_adder_5_s1), .a(a2), .b(b2));
  Half_Adder half_adder_6 (.s0(out_12), .s1(half_adder_6_s1), .a(half_adder_5_s0), .b(s11_out));
  or s11 (s11_out, half_adder_7_s1, half_adder_8_s1);
  Half_Adder half_adder_7 (.s0(out_13), .s1(half_adder_7_s1), .a(half_adder_8_s0), .b(1'b0));
  Half_Adder half_adder_8 (.s0(half_adder_8_s0), .s1(half_adder_8_s1), .a(a1), .b(b1));

  // Notes on the sheet:
  //   s14
  //   s04
  //   s13
  //   s03
  //   s12
  //   s02
  //   s11
  //   s01
endmodule

// HA
module Half_Adder (
  input  a,
  input  b,
  output s0,
  output s1
);

  xor xor_1 (s0, a, b);
  and and_1 (s1, a, b);
endmodule
