// Logisim project Guia_0802.circ as structural Verilog: 2 circuits, main circuit G08_02
module G08_02 (
  input  a4,
  input  a3,
  input  a2,
  input  a1,
  input  b4,
  input  b3,
  input  b2,
  input  b1,
  output out_9,
  output out_10,
  output out_11,
  output out_12,
  output out_13
);

  wire half_difference_1_s1, half_difference_2_s0, half_difference_2_s1, half_difference_3_s1,
       half_difference_4_s0, half_difference_4_s1, half_difference_5_s1, half_difference_6_s0,
       half_difference_6_s1, half_difference_7_s1, half_difference_8_s0, half_difference_8_s1, or_2_out,
       or_3_out, or_4_out;

  or or_1 (out_9, half_difference_1_s1, half_difference_2_s1);
  Half_Difference half_difference_1 (.s0(out_10), .s1(half_difference_1_s1), .a(half_difference_2_s0), .b(or_2_out));
  Half_Difference half_difference_2 (.s0(half_difference_2_s0), .s1(half_difference_2_s1), .a(a4), .b(b4));
  or or_2 (or_2_out, half_difference_3_s1, half_difference_4_s1);
  Half_Difference half_difference_3 (.s0(out_11), .s1(half_difference_3_s1), .a(half_difference_4_s0), .b(or_3_out));
  Half_Difference half_difference_4 (.s0(half_difference_4_s0), .s1(half_difference_4_s1), .a(a3), .b(b3));
  or or_3 (or_3_out, half_difference_5_s1, half_difference_6_s1);
  Half_Difference half_difference_5 (.s0(out_12), .s1(half_difference_5_s1), .a(half_difference_6_s0), .b(or_4_out));
  Half_Difference half_difference_6 (.s0(half_difference_6_s0), .s1(half_difference_6_s1), .a(a2), .b(b2));
  or or_4 (or_4_out, half_difference_7_s1, half_difference_8_s1);
  Half_Difference half_difference_7 (.s0(out_13), .s1(half_difference_7_s1), .a(half_difference_8_s0), .b(1'b0));
  Half_Difference half_difference_8 (.s0(half_difference_8_s0), .s1(half_difference_8_s1), .a(a1), .b(b1));

  // Notes on the sheet:
  //   s14
  //   s04
  //   s13
  //   s03
  //   s12
  //   s02
  //   s11
  //   s01
endmodule

// HD
module Half_Difference (
  input  a,
  input  b,
  output s0,
  output s1
);

  wire not_1_out;

  xor xor_1 (s0, a, b);
  not not_1 (not_1_out, a);
  and and_1 (s1, not_1_out, b);
endmodule
