// Logisim project Guia_0803.circ as structural Verilog: 1 circuit, main circuit G08_03
module G08_03 (
  input  a4,
  input  a3,
  input  a2,
  input  a1,
  input  b4,
  input  b3,
  input  b2,
  input  b1,
  output out_9
);

  wire and_2_out, and_3_out, and_4_out, xnor_1_out, xnor_2_out, xnor_3_out, xnor_4_out;

  and and_1 (out_9, xnor_1_out, and_2_out);
  xnor xnor_1 (xnor_1_out, a4, b4);
  and and_2 (and_2_out, xnor_2_out, and_3_out);
  xnor xnor_2 (xnor_2_out, a3, b3);
  and and_3 (and_3_out, xnor_3_out, and_4_out);
  xnor xnor_3 (xnor_3_out, a2, b2);
  and and_4 (and_4_out, xnor_4_out, 1'b1);
  xnor xnor_4 (xnor_4_out, a1, b1);
endmodule
