// Logisim project Guia_0804.circ as structural Verilog: 1 circuit, main circuit G08_04
module G08_04 (
  input  a4,
  input  a3,
  input  a2,
  input  a1,
  input  b4,
  input  b3,
  input  b2,
  input  b1,
  output out_9
);

  wire or_2_out, or_3_out, or_4_out, xor_1_out, xor_2_out, xor_3_out, xor_4_out;

  or or_1 (out_9, xor_1_out, or_2_out);
  xor xor_1 (xor_1_out, a4, b4);
  or or_2 (or_2_out, xor_2_out, or_3_out);
  xor xor_2 (xor_2_out, a3, b3);
  or or_3 (or_3_out, xor_3_out, or_4_out);
  xor xor_3 (xor_3_out, a2, b2);
  or or_4 (or_4_out, xor_4_out, 1'b0);
  xor xor_4 (xor_4_out, a1, b1);
endmodule
