// Logisim project Guia_0805.circ as structural Verilog: 3 circuits, main circuit G08_05
// a1
module G08_05 (
  input  a6,
  input  a5,
  input  a4,
  input  a3,
  input  a2,
  input  a1,
  output out_7,
  output out_8,
  output out_9,
  output out_10,
  output out_11,
  output out_12,
  output s16
);

  wire complemento_1_1_a1, complemento_1_1_b1, complemento_1_1_c1, complemento_1_1_d1, complemento_1_1_e1,
       complemento_1_1_f1, half_adder_1_s1, half_adder_2_s0, half_adder_2_s1, half_adder_3_s1,
       half_adder_4_s0, half_adder_4_s1, half_adder_5_s1, half_adder_6_s0, half_adder_6_s1, half_adder_7_s1,
       half_adder_8_s0, half_adder_8_s1, half_adder_9_s1, half_adder_10_s0, half_adder_10_s1,
       half_adder_11_s1, half_adder_12_s0, half_adder_12_s1, or_2_out, or_3_out, or_4_out, s11_2_out, s11_out;

  or or_1 (s16, half_adder_1_s1, half_adder_2_s1);
  Half_Adder half_adder_1 (.s0(out_7), .s1(half_adder_1_s1), .a(half_adder_2_s0), .b(s11_out));
  Half_Adder half_adder_2 (.s0(half_adder_2_s0), .s1(half_adder_2_s1), .a(complemento_1_1_f1), .b(1'b0));
  or s11 (s11_out, half_adder_3_s1, half_adder_4_s1);
  Half_Adder half_adder_3 (.s0(out_8), .s1(half_adder_3_s1), .a(half_adder_4_s0), .b(or_2_out));
  Half_Adder half_adder_4 (.s0(half_adder_4_s0), .s1(half_adder_4_s1), .a(complemento_1_1_e1), .b(1'b0));
  or or_2 (or_2_out, half_adder_5_s1, half_adder_6_s1);
  Half_Adder half_adder_5 (.s0(out_9), .s1(half_adder_5_s1), .a(half_adder_6_s0), .b(or_3_out));
  Half_Adder half_adder_6 (.s0(half_adder_6_s0), .s1(half_adder_6_s1), .a(complemento_1_1_d1), .b(1'b0));
  or or_3 (or_3_out, half_adder_7_s1, half_adder_8_s1);
  Half_Adder half_adder_7 (.s0(out_10), .s1(half_adder_7_s1), .a(half_adder_8_s0), .b(or_4_out));
  Half_Adder half_adder_8 (.s0(half_adder_8_s0), .s1(half_adder_8_s1), .a(complemento_1_1_c1), .b(1'b0));
  or or_4 (or_4_out, half_adder_9_s1, half_adder_10_s1);
  Half_Adder half_adder_9 (.s0(out_11), .s1(half_adder_9_s1), .a(half_adder_10_s0), .b(s11_2_out));
  Half_Adder half_adder_10 (.s0(half_adder_10_s0), .s1(half_adder_10_s1), .a(complemento_1_1_b1), .b(1'b0));
  or s11_2 (s11_2_out, half_adder_11_s1, half_adder_12_s1);
  Complemento_1 complemento_1_1 (
    .f(a6), .e(a5), .d(a4), .c(a3), .b(a2), .a(a1), .f1(complemento_1_1_f1), .e1(complemento_1_1_e1),
    .d1(complemento_1_1_d1), .c1(complemento_1_1_c1), .b1(complemento_1_1_b1), .a1(complemento_1_1_a1));
  Half_Adder half_adder_11 (.s0(out_12), .s1(half_adder_11_s1), .a(half_adder_12_s0), .b(1'b0));
  Half_Adder half_adder_12 (.s0(half_adder_12_s0), .s1(half_adder_12_s1), .a(complemento_1_1_a1), .b(1'b1));

  // Notes on the sheet:
  //   s06
  //   s15
  //   s05
  //   s14
  //   s04
  //   s13
  //   s03
  //   s12
  //   s02
  //   s11
  //   s01
endmodule

// HA
module Half_Adder (
  input  a,
  input  b,
  output s0,
  output s1
);

  xor xor_1 (s0, a, b);
  and and_1 (s1, a, b);
endmodule

// C1
module Complemento_1 (
  input  f,
  input  e,
  input  d,
  input  c,
  input  b,
  input  a,
  output f1,
  output e1,
  output d1,
  output c1,
  output b1,
  output a1
);

  not not_1 (f1, f);
  not not_2 (d1, d);
  not not_3 (e1, e);
  not not_4 (b1, b);
  not not_5 (c1, c);
  not not_6 (a1, a);
endmodule
