// Logisim project Guia_1102.circ as structural Verilog: 1 circuit, main circuit G11_02
module G11_02 (
  input  CLK,
  input  X,
  input  in_3,
  output out_4
);

  wire and_1_out, and_2_out, and_3_out, and_4_out, d_ff_1_q, d_ff_2_q, d_ff_2_qn, d_ff_3_q, d_ff_3_qn,
       not_1_out, or_1_out;

  and and_1 (and_1_out, X, or_1_out);
  or or_1 (or_1_out, d_ff_2_qn, d_ff_3_qn);
  D_Flip_Flop d_ff_1 (.clk(CLK), .D(and_1_out), .Q(d_ff_1_q), .reset(in_3));  // open: Qn, preset
  D_Flip_Flop d_ff_2 (.clk(CLK), .D(and_2_out), .Q(d_ff_2_q), .Qn(d_ff_2_qn), .reset(in_3));  // open: preset
  and and_2 (and_2_out, X, d_ff_1_q, d_ff_3_qn);
  not not_1 (not_1_out, X);
  and and_3 (and_3_out, not_1_out, d_ff_2_q);
  D_Flip_Flop d_ff_3 (.clk(CLK), .D(and_3_out), .Q(d_ff_3_q), .Qn(d_ff_3_qn), .reset(in_3));  // open: preset
  and and_4 (and_4_out, X, d_ff_3_q);
  D_Flip_Flop d_ff_4 (.clk(CLK), .D(and_4_out), .Q(out_4), .reset(in_3));  // open: Qn, preset
endmodule
