// Logisim project Guia_1103.circ as structural Verilog: 3 circuits, main circuit Moore
module G11_03 (
  input  Input,
  input  Clear,
  output Moore,
  output Mealy
);

  wire CLK_out;

  Clock CLK (.out(CLK_out));
  Moore moore_1 (.CLK(CLK_out), .Input(Input), .Clear(Clear), .Resultado(Moore));
  Mealy mealy_1 (.CLK(CLK_out), .Input(Input), .Clear(Clear), .Resultado(Mealy));
endmodule

// MO
module Moore (
  input  CLK,
  input  Input,
  input  Clear,
  output Resultado
);

  wire and_1_out, and_2_out, and_3_out, and_4_out, d_ff_1_q, d_ff_2_q, d_ff_2_qn, d_ff_3_q, d_ff_3_qn,
       not_1_out, or_1_out;

  and and_1 (and_1_out, Input, or_1_out);
  or or_1 (or_1_out, d_ff_2_qn, d_ff_3_qn);
  D_Flip_Flop d_ff_1 (.clk(CLK), .D(and_1_out), .Q(d_ff_1_q), .reset(Clear));  // open: Qn, preset
  D_Flip_Flop d_ff_2 (.clk(CLK), .D(and_2_out), .Q(d_ff_2_q), .Qn(d_ff_2_qn), .reset(Clear));  // open: preset
  and and_2 (and_2_out, Input, d_ff_1_q, d_ff_3_qn);
  not not_1 (not_1_out, Input);
  and and_3 (and_3_out, not_1_out, d_ff_2_q);
  D_Flip_Flop d_ff_3 (.clk(CLK), .D(and_3_out), .Q(d_ff_3_q), .Qn(d_ff_3_qn), .reset(Clear));  // open: preset
  and and_4 (and_4_out, Input, d_ff_3_q);
  D_Flip_Flop d_ff_4 (.clk(CLK), .D(and_4_out), .Q(Resultado), .reset(Clear));  // open: Qn, preset
endmodule

// ME
module Mealy (
  input  CLK,
  input  Input,
  input  Clear,
  output Resultado
);

  wire and_1_out, and_2_out, and_3_out, and_4_out, d_ff_1_q, d_ff_2_q, d_ff_2_qn, d_ff_3_q, d_ff_3_qn,
       not_1_out;

  and and_1 (and_1_out, Input, d_ff_3_qn, d_ff_2_qn);
  D_Flip_Flop d_ff_1 (.clk(CLK), .D(and_1_out), .Q(d_ff_1_q), .reset(Clear));  // open: Qn, preset
  D_Flip_Flop d_ff_2 (.clk(CLK), .D(and_2_out), .Q(d_ff_2_q), .Qn(d_ff_2_qn), .reset(Clear));  // open: preset
  and and_2 (and_2_out, Input, d_ff_1_q, d_ff_3_qn);
  not not_1 (not_1_out, Input);
  and and_3 (and_3_out, not_1_out, d_ff_2_q);
  D_Flip_Flop d_ff_3 (.clk(CLK), .D(and_3_out), .Q(d_ff_3_q), .Qn(d_ff_3_qn), .reset(Clear));  // open: preset
  and and_4 (and_4_out, Input, d_ff_3_q);
  D_Flip_Flop d_ff_4 (.clk(CLK), .D(and_4_out), .Q(Resultado), .reset(Clear));  // open: Qn, preset
endmodule
