// Logisim project Guia_1201.circ as structural Verilog: 2 circuits, main circuit G12_01
module G12_01 (
  input  Address,
  input  R_W,
  input  Input1,
  input  Input2,
  input  Input3,
  input  Clear,
  input  Input4,
  output Output1,
  output Output2,
  output Output3,
  output Output4
);

  wire CLK_out;

  Clock CLK (.out(CLK_out));
  RAM_1X1__JK ram_1x1_jk_1 (.Address(Address), .R_W(R_W), .CLK(CLK_out), .Input(Input1), .CLR(Clear), .Output(Output1));
  RAM_1X1__JK ram_1x1_jk_2 (.Address(Address), .R_W(R_W), .CLK(CLK_out), .Input(Input2), .CLR(Clear), .Output(Output2));
  RAM_1X1__JK ram_1x1_jk_3 (.Address(Address), .R_W(R_W), .CLK(CLK_out), .Input(Input3), .CLR(Clear), .Output(Output3));
  RAM_1X1__JK ram_1x1_jk_4 (.Address(Address), .R_W(R_W), .CLK(CLK_out), .Input(Input4), .CLR(Clear), .Output(Output4));
endmodule

// 1X1
module RAM_1X1__JK (
  input  Address,
  input  R_W,
  input  CLK,
  input  Input,
  input  CLR,
  output Output
);

  wire and_1_out, demultiplexer_1_out0, demultiplexer_1_out1, j_k_ff_1_q, multiplexer_1_out, not_1_out;

  Demultiplexer #(.enable("false")) demultiplexer_1 (
    .out0(demultiplexer_1_out0), .out1(demultiplexer_1_out1), .in(Input), .sel(j_k_ff_1_q));
  and and_1 (and_1_out, Address, R_W, CLK);
  Multiplexer #(.enable("false")) multiplexer_1 (
    .in0(demultiplexer_1_out0), .in1(not_1_out), .out(multiplexer_1_out), .sel(j_k_ff_1_q));
  not not_1 (not_1_out, demultiplexer_1_out1);
  J_K_Flip_Flop j_k_ff_1 (
    .J(Input), .clk(and_1_out), .K(multiplexer_1_out), .Q(j_k_ff_1_q), .reset(CLR));  // open: Qn, preset
  and and_2 (Output, Address, j_k_ff_1_q);
endmodule
