// Logisim project Guia_1202.circ as structural Verilog: 4 circuits, main circuit RAM 1X4
module G12_02 (
  input  Address,
  input  R_W,
  input  Input1,
  input  Input2,
  input  Input3,
  input  Input4,
  input  Input5,
  input  Input6,
  input  Input7,
  input  Input8,
  input  Clear,
  output Output1,
  output Output2,
  output Output3,
  output Output4,
  output Output5,
  output Output6,
  output Output7,
  output Output8
);

  wire CLK_out;

  Clock CLK (.out(CLK_out));
  RAM_1X4 ram_1x4_1 (
    .Address(Address), .R_W(R_W), .CLK(CLK_out), .Input1(Input1), .Input2(Input2), .Input3(Input3),
    .Input4(Input4), .Clear(Clear), .Output1(Output1), .Output2(Output2), .Output3(Output3), .Output4(Output4));
  RAM_1X4 ram_1x4_2 (
    .Address(Address), .R_W(R_W), .CLK(CLK_out), .Input1(Input5), .Input2(Input6), .Input3(Input7),
    .Input4(Input8), .Clear(Clear), .Output1(Output5), .Output2(Output6), .Output3(Output7), .Output4(Output8));
endmodule

// 1X4
module RAM_1X4 (
  input  Address,
  input  R_W,
  input  CLK,
  input  Input1,
  input  Input2,
  input  Input3,
  input  Clear,
  input  Input4,
  output Output1,
  output Output2,
  output Output3,
  output Output4
);

  RAM_1X1__JK ram_1x1_jk_1 (.Address(Address), .R_W(R_W), .CLK(CLK), .Input(Input1), .CLR(Clear), .Output(Output1));
  RAM_1X1__JK ram_1x1_jk_2 (.Address(Address), .R_W(R_W), .CLK(CLK), .Input(Input2), .CLR(Clear), .Output(Output2));
  RAM_1X1__JK ram_1x1_jk_3 (.Address(Address), .R_W(R_W), .CLK(CLK), .Input(Input3), .CLR(Clear), .Output(Output3));
  RAM_1X1__JK ram_1x1_jk_4 (.Address(Address), .R_W(R_W), .CLK(CLK), .Input(Input4), .CLR(Clear), .Output(Output4));
endmodule

// 1X1
module RAM_1X1__JK (
  input  Address,
  input  R_W,
  input  CLK,
  input  Input,
  input  CLR,
  output Output
);

  wire and_1_out, demultiplexer_1_out0, demultiplexer_1_out1, j_k_ff_1_q, multiplexer_1_out, not_1_out;

  Demultiplexer #(.enable("false")) demultiplexer_1 (
    .out0(demultiplexer_1_out0), .out1(demultiplexer_1_out1), .in(Input), .sel(j_k_ff_1_q));
  and and_1 (and_1_out, Address, R_W, CLK);
  Multiplexer #(.enable("false")) multiplexer_1 (
    .in0(demultiplexer_1_out0), .in1(not_1_out), .out(multiplexer_1_out), .sel(j_k_ff_1_q));
  not not_1 (not_1_out, demultiplexer_1_out1);
  J_K_Flip_Flop j_k_ff_1 (
    .J(Input), .clk(and_1_out), .K(multiplexer_1_out), .Q(j_k_ff_1_q), .reset(CLR));  // open: Qn, preset
  and and_2 (Output, Address, j_k_ff_1_q);
endmodule

// 1X1
module RAM_1X1 (
  input  Address,
  input  R_W,
  input  CLK,
  input  Input,
  input  CLR,
  output Output
);

  wire and_1_out, d_ff_1_q;

  and and_1 (and_1_out, Address, R_W, CLK);
  D_Flip_Flop #(.Pre_Clr_Positions("LEGACY"), .enable("true")) d_ff_1 (
    .clk(and_1_out), .D(Input), .Q(d_ff_1_q), .reset(CLR));  // open: Qn, preset, en
  and and_2 (Output, Address, d_ff_1_q);
endmodule
