// Logisim project Guia_1203.circ as structural Verilog: 4 circuits, main circuit G12_03
module G12_03 (
  input  Address,
  input  R_W,
  input  [7:0] Input,
  input  Clear,
  output [7:0] Output
);

  wire CLK_out, demultiplexer_1_out0, demultiplexer_1_out1;
  wire [7:0] ram_1x8_1_output, ram_1x8_2_output;

  Demultiplexer #(.enable("false")) demultiplexer_1 (
    .out0(demultiplexer_1_out0), .out1(demultiplexer_1_out1), .in(1'b1), .sel(Address));
  Clock CLK (.out(CLK_out));
  RAM_1X8 ram_1x8_1 (
    .Address(demultiplexer_1_out1), .R_W(R_W), .CLK(CLK_out), .Input(Input), .Clear(Clear),
    .Output(ram_1x8_1_output));
  RAM_1X8 ram_1x8_2 (
    .Address(demultiplexer_1_out0), .R_W(R_W), .CLK(CLK_out), .Input(Input), .Clear(Clear),
    .Output(ram_1x8_2_output));
  Multiplexer #(.width(8), .enable("false")) multiplexer_1 (
    .in0(ram_1x8_2_output), .in1(ram_1x8_1_output), .out(Output), .sel(Address));
endmodule

// 1X8
module RAM_1X8 (
  input  Address,
  input  R_W,
  input  CLK,
  input  [7:0] Input,
  input  Clear,
  output [7:0] Output
);

  RAM_1X4 ram_1x4_1 (.Address(Address), .R_W(R_W), .CLK(CLK), .Input(Input[3:0]), .Clear(Clear), .out_6(Output[3:0]));
  RAM_1X4 ram_1x4_2 (.Address(Address), .R_W(R_W), .CLK(CLK), .Input(Input[7:4]), .Clear(Clear), .out_6(Output[7:4]));
endmodule

// 1X4
module RAM_1X4 (
  input  Address,
  input  R_W,
  input  CLK,
  input  [3:0] Input,
  input  Clear,
  output [3:0] out_6
);

  RAM_1X1 ram_1x1_1 (.Address(Address), .R_W(R_W), .CLK(CLK), .Input(Input[0]), .CLR(Clear), .Output(out_6[0]));
  RAM_1X1 ram_1x1_2 (.Address(Address), .R_W(R_W), .CLK(CLK), .Input(Input[1]), .CLR(Clear), .Output(out_6[1]));
  RAM_1X1 ram_1x1_3 (.Address(Address), .R_W(R_W), .CLK(CLK), .Input(Input[2]), .CLR(Clear), .Output(out_6[2]));
  RAM_1X1 ram_1x1_4 (.Address(Address), .R_W(R_W), .CLK(CLK), .Input(Input[3]), .CLR(Clear), .Output(out_6[3]));
endmodule

// 1X1
module RAM_1X1 (
  input  Address,
  input  R_W,
  input  CLK,
  input  Input,
  input  CLR,
  output Output
);

  wire and_1_out, demultiplexer_1_out0, demultiplexer_1_out1, j_k_ff_1_q, multiplexer_1_out, not_1_out;

  Demultiplexer #(.enable("false")) demultiplexer_1 (
    .out0(demultiplexer_1_out0), .out1(demultiplexer_1_out1), .in(Input), .sel(j_k_ff_1_q));
  and and_1 (and_1_out, Address, R_W, CLK);
  Multiplexer #(.enable("false")) multiplexer_1 (
    .in0(demultiplexer_1_out0), .in1(not_1_out), .out(multiplexer_1_out), .sel(j_k_ff_1_q));
  not not_1 (not_1_out, demultiplexer_1_out1);
  J_K_Flip_Flop j_k_ff_1 (
    .J(Input), .clk(and_1_out), .K(multiplexer_1_out), .Q(j_k_ff_1_q), .reset(CLR));  // open: Qn, preset
  and and_2 (Output, Address, j_k_ff_1_q);
endmodule
