// Logisim project Guia_1207.circ as structural Verilog: 5 circuits, main circuit RAM 1X8
module G12_07 (
  input  [2:0] Address,
  input  R_W,
  input  [15:0] in_3,
  input  Clear,
  output [15:0] out_5
);

  wire CLK_out, demultiplexer_1_out0, demultiplexer_1_out1, demultiplexer_1_out2, demultiplexer_1_out3,
       demultiplexer_1_out4, demultiplexer_1_out5, demultiplexer_1_out6, demultiplexer_1_out7;
  wire [15:0] ram_1x16_1_output, ram_1x16_2_output, ram_1x16_3_output, ram_1x16_4_output, ram_1x16_5_output,
       ram_1x16_6_output, ram_1x16_7_output, ram_1x16_8_output;

  Clock CLK (.out(CLK_out));
  RAM_1X16 ram_1x16_1 (
    .R_W(R_W), .CLK(CLK_out), .Input(in_3), .Address(demultiplexer_1_out0), .Clear(Clear),
    .Output(ram_1x16_1_output));
  RAM_1X16 ram_1x16_2 (
    .R_W(R_W), .CLK(CLK_out), .Input(in_3), .Address(demultiplexer_1_out1), .Clear(Clear),
    .Output(ram_1x16_2_output));
  RAM_1X16 ram_1x16_3 (
    .R_W(R_W), .CLK(CLK_out), .Input(in_3), .Address(demultiplexer_1_out2), .Clear(Clear),
    .Output(ram_1x16_3_output));
  RAM_1X16 ram_1x16_4 (
    .R_W(R_W), .CLK(CLK_out), .Input(in_3), .Address(demultiplexer_1_out3), .Clear(Clear),
    .Output(ram_1x16_4_output));
  Demultiplexer #(.select(3), .enable("false")) demultiplexer_1 (
    .out0(demultiplexer_1_out0), .out1(demultiplexer_1_out1), .out2(demultiplexer_1_out2),
    .out3(demultiplexer_1_out3), .out4(demultiplexer_1_out4), .out5(demultiplexer_1_out5),
    .out6(demultiplexer_1_out6), .out7(demultiplexer_1_out7), .in(1'b1), .sel(Address));
  RAM_1X16 ram_1x16_5 (
    .R_W(R_W), .CLK(CLK_out), .Input(in_3), .Address(demultiplexer_1_out4), .Clear(Clear),
    .Output(ram_1x16_5_output));
  RAM_1X16 ram_1x16_6 (
    .R_W(R_W), .CLK(CLK_out), .Input(in_3), .Address(demultiplexer_1_out5), .Clear(Clear),
    .Output(ram_1x16_6_output));
  RAM_1X16 ram_1x16_7 (
    .R_W(R_W), .CLK(CLK_out), .Input(in_3), .Address(demultiplexer_1_out6), .Clear(Clear),
    .Output(ram_1x16_7_output));
  RAM_1X16 ram_1x16_8 (
    .R_W(R_W), .CLK(CLK_out), .Input(in_3), .Address(demultiplexer_1_out7), .Clear(Clear),
    .Output(ram_1x16_8_output));
  Multiplexer #(.select(3), .width(16), .enable("false")) multiplexer_1 (
    .in0(ram_1x16_1_output), .in1(ram_1x16_2_output), .in2(ram_1x16_3_output), .in3(ram_1x16_4_output),
    .in4(ram_1x16_5_output), .in5(ram_1x16_6_output), .in6(ram_1x16_7_output), .in7(ram_1x16_8_output),
    .out(out_5), .sel(Address));
endmodule

// 1X16
module RAM_1X16 (
  input  Address,
  input  R_W,
  input  CLK,
  input  [15:0] Input,
  input  Clear,
  output [15:0] Output
);

  RAM_1X8 ram_1x8_1 (.Address(Address), .R_W(R_W), .CLK(CLK), .Input(Input[7:0]), .Clear(Clear), .Output(Output[7:0]));
  RAM_1X8 ram_1x8_2 (
    .Address(Address), .R_W(R_W), .CLK(CLK), .Input(Input[15:8]), .Clear(Clear), .Output(Output[15:8]));
endmodule

// 1X8
module RAM_1X8 (
  input  Address,
  input  R_W,
  input  CLK,
  input  [7:0] Input,
  input  Clear,
  output [7:0] Output
);

  RAM_1X4 ram_1x4_1 (.Address(Address), .R_W(R_W), .CLK(CLK), .Input(Input[3:0]), .Clear(Clear), .out_6(Output[3:0]));
  RAM_1X4 ram_1x4_2 (.Address(Address), .R_W(R_W), .CLK(CLK), .Input(Input[7:4]), .Clear(Clear), .out_6(Output[7:4]));
endmodule

// 1X4
module RAM_1X4 (
  input  Address,
  input  R_W,
  input  CLK,
  input  [3:0] Input,
  input  Clear,
  output [3:0] out_6
);

  RAM_1X1 ram_1x1_1 (.Address(Address), .R_W(R_W), .CLK(CLK), .Input(Input[0]), .CLR(Clear), .Output(out_6[0]));
  RAM_1X1 ram_1x1_2 (.Address(Address), .R_W(R_W), .CLK(CLK), .Input(Input[1]), .CLR(Clear), .Output(out_6[1]));
  RAM_1X1 ram_1x1_3 (.Address(Address), .R_W(R_W), .CLK(CLK), .Input(Input[2]), .CLR(Clear), .Output(out_6[2]));
  RAM_1X1 ram_1x1_4 (.Address(Address), .R_W(R_W), .CLK(CLK), .Input(Input[3]), .CLR(Clear), .Output(out_6[3]));
endmodule

// 1X1
module RAM_1X1 (
  input  Address,
  input  R_W,
  input  CLK,
  input  Input,
  input  CLR,
  output Output
);

  wire and_1_out, demultiplexer_1_out0, demultiplexer_1_out1, j_k_ff_1_q, multiplexer_1_out, not_1_out;

  Demultiplexer #(.enable("false")) demultiplexer_1 (
    .out0(demultiplexer_1_out0), .out1(demultiplexer_1_out1), .in(Input), .sel(j_k_ff_1_q));
  and and_1 (and_1_out, Address, R_W, CLK);
  Multiplexer #(.enable("false")) multiplexer_1 (
    .in0(demultiplexer_1_out0), .in1(not_1_out), .out(multiplexer_1_out), .sel(j_k_ff_1_q));
  not not_1 (not_1_out, demultiplexer_1_out1);
  J_K_Flip_Flop j_k_ff_1 (
    .J(Input), .clk(and_1_out), .K(multiplexer_1_out), .Q(j_k_ff_1_q), .reset(CLR));  // open: Qn, preset
  and and_2 (Output, Address, j_k_ff_1_q);
endmodule
