// Logisim project Guia_1301.circ as structural Verilog: 1 circuit, main circuit G13_01
// 1X1
module G13_01 (
  input  _1,
  input  Clear,
  output A,
  output B,
  output C,
  output D,
  output E
);

  wire Pulse_out;

  Clock Pulse (.out(Pulse_out));
  J_K_Flip_Flop j_k_ff_1 (.J(_1), .clk(B), .K(_1), .Qn(A), .reset(Clear));  // open: Q, preset
  J_K_Flip_Flop j_k_ff_2 (.J(_1), .clk(C), .K(_1), .Qn(B), .reset(Clear));  // open: Q, preset
  J_K_Flip_Flop j_k_ff_3 (.J(_1), .clk(D), .K(_1), .Qn(C), .reset(Clear));  // open: Q, preset
  J_K_Flip_Flop j_k_ff_4 (.J(_1), .clk(E), .K(_1), .Qn(D), .reset(Clear));  // open: Q, preset
  J_K_Flip_Flop j_k_ff_5 (.J(_1), .clk(Pulse_out), .K(_1), .Qn(E), .reset(Clear));  // open: Q, preset
endmodule
