// Logisim project Guia_1302.circ as structural Verilog: 1 circuit, main circuit G13_02
// 1X1
module G13_02 (
  input  _1,
  input  Clear,
  output A,
  output B,
  output C,
  output D,
  output E
);

  wire j_k_ff_2_q, j_k_ff_3_q, j_k_ff_4_q, j_k_ff_5_q, Pulse_out;

  Clock Pulse (.out(Pulse_out));
  J_K_Flip_Flop j_k_ff_1 (.J(_1), .clk(j_k_ff_2_q), .K(_1), .Qn(A), .reset(Clear));  // open: Q, preset
  J_K_Flip_Flop j_k_ff_2 (.J(_1), .clk(j_k_ff_3_q), .K(_1), .Q(j_k_ff_2_q), .Qn(B), .reset(Clear));  // open: preset
  J_K_Flip_Flop j_k_ff_3 (.J(_1), .clk(j_k_ff_4_q), .K(_1), .Q(j_k_ff_3_q), .Qn(C), .reset(Clear));  // open: preset
  J_K_Flip_Flop j_k_ff_4 (.J(_1), .clk(j_k_ff_5_q), .K(_1), .Q(j_k_ff_4_q), .Qn(D), .reset(Clear));  // open: preset
  J_K_Flip_Flop j_k_ff_5 (.J(_1), .clk(Pulse_out), .K(_1), .Q(j_k_ff_5_q), .Qn(E), .reset(Clear));  // open: preset
endmodule
