// Logisim project Guia_1303.circ as structural Verilog: 1 circuit, main circuit G13_03
// 1X1
module G13_03 (
  input  in_1,
  input  Clear,
  output A,
  output B,
  output C,
  output D
);

  wire and_1_out, j_k_ff_1_qn, j_k_ff_2_qn, j_k_ff_3_qn, not_1_out, not_2_out, or_1_out, Pulse_out;

  Clock Pulse (.out(Pulse_out));
  or or_1 (or_1_out, Clear, and_1_out);
  not not_1 (not_1_out, D);
  and and_1 (and_1_out, not_1_out, C, not_2_out, A);
  not not_2 (not_2_out, B);
  J_K_Flip_Flop j_k_ff_1 (
    .J(in_1), .clk(Pulse_out), .K(in_1), .Q(D), .Qn(j_k_ff_1_qn), .reset(or_1_out));  // open: preset
  J_K_Flip_Flop j_k_ff_2 (
    .J(in_1), .clk(j_k_ff_1_qn), .K(in_1), .Q(C), .Qn(j_k_ff_2_qn), .reset(or_1_out));  // open: preset
  J_K_Flip_Flop j_k_ff_3 (
    .J(in_1), .clk(j_k_ff_2_qn), .K(in_1), .Q(B), .Qn(j_k_ff_3_qn), .reset(or_1_out));  // open: preset
  J_K_Flip_Flop j_k_ff_4 (.J(in_1), .clk(j_k_ff_3_qn), .K(in_1), .Q(A), .reset(or_1_out));  // open: Qn, preset
endmodule
