// Logisim project Guia_1304.circ as structural Verilog: 1 circuit, main circuit G13_04
// 1X1
module G13_04 (
  input  _1,
  input  Clear,
  output A,
  output B,
  output C,
  output D
);

  wire and_1_out, j_k_ff_1_qn, j_k_ff_2_qn, j_k_ff_3_qn, j_k_ff_4_qn, not_1_out, not_2_out, or_1_out,
       Pulse_out;

  Clock Pulse (.out(Pulse_out));
  or or_1 (or_1_out, Clear, and_1_out);
  not not_1 (not_1_out, j_k_ff_1_qn);
  and and_1 (and_1_out, not_1_out, j_k_ff_2_qn, not_2_out, j_k_ff_4_qn);
  not not_2 (not_2_out, j_k_ff_3_qn);
  J_K_Flip_Flop j_k_ff_1 (.J(_1), .clk(Pulse_out), .K(_1), .Q(D), .Qn(j_k_ff_1_qn), .reset(or_1_out));  // open: preset
  J_K_Flip_Flop j_k_ff_2 (.J(_1), .clk(D), .K(_1), .Q(C), .Qn(j_k_ff_2_qn), .reset(or_1_out));  // open: preset
  J_K_Flip_Flop j_k_ff_3 (.J(_1), .clk(C), .K(_1), .Q(B), .Qn(j_k_ff_3_qn), .reset(or_1_out));  // open: preset
  J_K_Flip_Flop j_k_ff_4 (.J(_1), .clk(B), .K(_1), .Q(A), .Qn(j_k_ff_4_qn), .reset(or_1_out));  // open: preset
endmodule
