// Logisim project Guia_1305.circ as structural Verilog: 1 circuit, main circuit G13_05
// 1X1
module G13_05 (
  input  _1,
  input  Clear,
  output A,
  output B,
  output C,
  output D,
  output E,
  output F,
  output G
);

  wire and_1_out, and_2_out, and_3_out, and_4_out, and_5_out, Pulse_out;

  Clock Pulse (.out(Pulse_out));
  T_Flip_Flop t_ff_1 (.clk(Pulse_out), .T(_1), .Q(G), .reset(Clear));  // open: Qn, preset
  T_Flip_Flop t_ff_2 (.clk(Pulse_out), .T(G), .Q(F), .reset(Clear));  // open: Qn, preset
  and and_1 (and_1_out, G, F);
  T_Flip_Flop t_ff_3 (.clk(Pulse_out), .T(and_1_out), .Q(E), .reset(Clear));  // open: Qn, preset
  and and_2 (and_2_out, and_1_out, E);
  T_Flip_Flop t_ff_4 (.clk(Pulse_out), .T(and_2_out), .Q(D), .reset(Clear));  // open: Qn, preset
  and and_3 (and_3_out, and_2_out, D);
  T_Flip_Flop t_ff_5 (.clk(Pulse_out), .T(and_3_out), .Q(C), .reset(Clear));  // open: Qn, preset
  and and_4 (and_4_out, and_3_out, C);
  T_Flip_Flop t_ff_6 (.clk(Pulse_out), .T(and_4_out), .Q(B), .reset(Clear));  // open: Qn, preset
  and and_5 (and_5_out, and_4_out, B);
  T_Flip_Flop t_ff_7 (.clk(Pulse_out), .T(and_5_out), .Q(A), .reset(Clear));  // open: Qn, preset
endmodule
