// Logisim project Guia_1402.circ as structural Verilog: 1 circuit, main circuit G14_02
// 1X1
module G14_02 (
  input  Data,
  input  Clear,
  input  Load,
  output A,
  output B,
  output C,
  output D,
  output E,
  output F
);

  wire CLK_out, multiplexer_1_out, multiplexer_2_out, multiplexer_3_out, multiplexer_4_out,
       multiplexer_5_out, multiplexer_6_out;

  Clock CLK (.out(CLK_out));
  D_Flip_Flop #(.Pre_Clr_Positions("LEGACY")) d_ff_1 (
    .clk(CLK_out), .D(B), .Q(A), .preset(multiplexer_1_out), .reset(Clear));  // open: Qn
  Multiplexer #(.enable("false")) multiplexer_1 (.in0(Load), .in1(1'b1), .out(multiplexer_1_out), .sel(Load));
  D_Flip_Flop #(.Pre_Clr_Positions("LEGACY")) d_ff_2 (
    .clk(CLK_out), .D(C), .Q(B), .preset(multiplexer_2_out), .reset(Clear));  // open: Qn
  Multiplexer #(.enable("false")) multiplexer_2 (.in0(Load), .in1(1'b1), .out(multiplexer_2_out), .sel(Load));
  Multiplexer #(.enable("false")) multiplexer_3 (.in0(Load), .in1(1'b1), .out(multiplexer_3_out), .sel(Load));
  D_Flip_Flop #(.Pre_Clr_Positions("LEGACY")) d_ff_3 (
    .clk(CLK_out), .D(D), .Q(C), .preset(multiplexer_3_out), .reset(Clear));  // open: Qn
  D_Flip_Flop #(.Pre_Clr_Positions("LEGACY")) d_ff_4 (
    .clk(CLK_out), .D(E), .Q(D), .preset(multiplexer_4_out), .reset(Clear));  // open: Qn
  Multiplexer #(.enable("false")) multiplexer_4 (.in0(Load), .in1(1'b1), .out(multiplexer_4_out), .sel(Load));
  Multiplexer #(.enable("false")) multiplexer_5 (.in0(Load), .in1(1'b1), .out(multiplexer_5_out), .sel(Load));
  D_Flip_Flop #(.Pre_Clr_Positions("LEGACY")) d_ff_5 (
    .clk(CLK_out), .D(F), .Q(E), .preset(multiplexer_5_out), .reset(Clear));  // open: Qn
  Multiplexer #(.enable("false")) multiplexer_6 (.in0(Load), .in1(1'b1), .out(multiplexer_6_out), .sel(Load));
  D_Flip_Flop #(.Pre_Clr_Positions("LEGACY")) d_ff_6 (
    .clk(CLK_out), .D(Data), .Q(F), .preset(multiplexer_6_out), .reset(Clear));  // open: Qn
endmodule
