// Logisim project Guia_1403.circ as structural Verilog: 2 circuits, main circuit G14_03
// 1X1
module G14_03 (
  input  Clear,
  output A,
  output B,
  output C,
  output D,
  output E,
  output F
);

  wire CLK_out;

  Clock CLK (.out(CLK_out));
  D_Flip_Flop #(.Pre_Clr_Positions("LEGACY")) d_ff_1 (.clk(CLK_out), .D(F), .Q(A), .preset(Clear));  // open: Qn, reset
  D_Flip_Flop #(.Pre_Clr_Positions("LEGACY")) d_ff_2 (.clk(CLK_out), .D(A), .Q(B), .reset(Clear));  // open: Qn, preset
  D_Flip_Flop #(.Pre_Clr_Positions("LEGACY")) d_ff_3 (.clk(CLK_out), .D(B), .Q(C), .reset(Clear));  // open: Qn, preset
  D_Flip_Flop #(.Pre_Clr_Positions("LEGACY")) d_ff_4 (.clk(CLK_out), .D(C), .Q(D), .reset(Clear));  // open: Qn, preset
  D_Flip_Flop #(.Pre_Clr_Positions("LEGACY")) d_ff_5 (.clk(CLK_out), .D(D), .Q(E), .reset(Clear));  // open: Qn, preset
  D_Flip_Flop #(.Pre_Clr_Positions("LEGACY")) d_ff_6 (.clk(CLK_out), .D(E), .Q(F), .reset(Clear));  // open: Qn, preset
endmodule

module G14_03_2 (
  input  Clear,
  input  Load,
  output A,
  output B,
  output C,
  output D,
  output E,
  output F
);

  wire CLK_out, or_1_out, or_2_out, or_3_out, or_4_out, or_5_out;

  Clock CLK (.out(CLK_out));
  D_Flip_Flop #(.Pre_Clr_Positions("LEGACY")) d_ff_1 (
    .clk(CLK_out), .D(F), .Q(A), .preset(Load), .reset(Clear));  // open: Qn
  D_Flip_Flop #(.Pre_Clr_Positions("LEGACY")) d_ff_2 (
    .clk(CLK_out), .D(A), .Q(B), .reset(or_1_out));  // open: Qn, preset
  or or_1 (or_1_out, Clear, Load);
  D_Flip_Flop #(.Pre_Clr_Positions("LEGACY")) d_ff_3 (
    .clk(CLK_out), .D(B), .Q(C), .reset(or_2_out));  // open: Qn, preset
  or or_2 (or_2_out, Clear, Load);
  D_Flip_Flop #(.Pre_Clr_Positions("LEGACY")) d_ff_4 (
    .clk(CLK_out), .D(C), .Q(D), .reset(or_3_out));  // open: Qn, preset
  or or_3 (or_3_out, Clear, Load);
  or or_4 (or_4_out, Clear, Load);
  D_Flip_Flop #(.Pre_Clr_Positions("LEGACY")) d_ff_5 (
    .clk(CLK_out), .D(D), .Q(E), .reset(or_4_out));  // open: Qn, preset
  D_Flip_Flop #(.Pre_Clr_Positions("LEGACY")) d_ff_6 (
    .clk(CLK_out), .D(E), .Q(F), .reset(or_5_out));  // open: Qn, preset
  or or_5 (or_5_out, Clear, Load);
endmodule
