// Logisim project Guia_1404.circ as structural Verilog: 1 circuit, main circuit G14_04
// 1X1
module G14_04 (
  input  Input,
  input  Clear,
  output A,
  output B,
  output C,
  output D,
  output E,
  output F
);

  wire CLK_out, or_1_out;

  Clock CLK (.out(CLK_out));
  or or_1 (or_1_out, Input, F);
  D_Flip_Flop #(.Pre_Clr_Positions("LEGACY")) d_ff_1 (
    .clk(CLK_out), .D(or_1_out), .Q(A), .reset(Clear));  // open: Qn, preset
  D_Flip_Flop #(.Pre_Clr_Positions("LEGACY")) d_ff_2 (.clk(CLK_out), .D(A), .Q(B), .reset(Clear));  // open: Qn, preset
  D_Flip_Flop #(.Pre_Clr_Positions("LEGACY")) d_ff_3 (.clk(CLK_out), .D(B), .Q(C), .reset(Clear));  // open: Qn, preset
  D_Flip_Flop #(.Pre_Clr_Positions("LEGACY")) d_ff_4 (.clk(CLK_out), .D(C), .Q(D), .reset(Clear));  // open: Qn, preset
  D_Flip_Flop #(.Pre_Clr_Positions("LEGACY")) d_ff_5 (.clk(CLK_out), .D(D), .Q(E), .reset(Clear));  // open: Qn, preset
  D_Flip_Flop #(.Pre_Clr_Positions("LEGACY")) d_ff_6 (.clk(CLK_out), .D(E), .Q(F), .reset(Clear));  // open: Qn, preset
endmodule
