// Logisim project Guia_1405.circ as structural Verilog: 1 circuit, main circuit G14_05
// 1X1
module G14_05 (
  input  Input,
  input  Clear,
  input  Load,
  input  in_4,
  input  in_5,
  input  in_6,
  input  in_7,
  input  in_8,
  input  in_9,
  output A,
  output B,
  output C,
  output D,
  output E,
  output F
);

  wire and_1_out, and_2_out, and_3_out, and_4_out, and_5_out, and_6_out, CLK_out;

  Clock CLK (.out(CLK_out));
  D_Flip_Flop #(.Pre_Clr_Positions("LEGACY")) d_ff_1 (
    .clk(CLK_out), .D(Input), .Q(A), .preset(and_1_out), .reset(Clear));  // open: Qn
  and and_1 (and_1_out, Load, in_4);
  and and_2 (and_2_out, Load, in_5);
  D_Flip_Flop #(.Pre_Clr_Positions("LEGACY")) d_ff_2 (
    .clk(CLK_out), .D(A), .Q(B), .preset(and_2_out), .reset(Clear));  // open: Qn
  D_Flip_Flop #(.Pre_Clr_Positions("LEGACY")) d_ff_3 (
    .clk(CLK_out), .D(B), .Q(C), .preset(and_3_out), .reset(Clear));  // open: Qn
  and and_3 (and_3_out, Load, in_6);
  D_Flip_Flop #(.Pre_Clr_Positions("LEGACY")) d_ff_4 (
    .clk(CLK_out), .D(C), .Q(D), .preset(and_4_out), .reset(Clear));  // open: Qn
  and and_4 (and_4_out, Load, in_7);
  and and_5 (and_5_out, Load, in_8);
  D_Flip_Flop #(.Pre_Clr_Positions("LEGACY")) d_ff_5 (
    .clk(CLK_out), .D(D), .Q(E), .preset(and_5_out), .reset(Clear));  // open: Qn
  D_Flip_Flop #(.Pre_Clr_Positions("LEGACY")) d_ff_6 (
    .clk(CLK_out), .D(E), .Q(F), .preset(and_6_out), .reset(Clear));  // open: Qn
  and and_6 (and_6_out, Load, in_9);
endmodule
